// Logisim project FinalCirc.circ as structural Verilog
module _8_bit_ALU (
  input  [7:0] A,
  input  [7:0] B,
  input  [1:0] ALU_Op,
  output [7:0] ALU_Out
);

  wire and_1_out;
  wire [7:0] adder_1_out, and_2_out, multiplexer_1_out, not_1_out, or_1_out;

  Multiplexer #(.width(8), .enable("false")) multiplexer_1 (
    .in0(B), .in1(not_1_out), .out(multiplexer_1_out), .sel(and_1_out));
  assign not_1_out = ~B;  // NOT_Gate not_1, 8 bits wide
  and and_1 (and_1_out, ALU_Op[0], ALU_Op[1]);
  Adder adder_1 (.a(A), .b(multiplexer_1_out), .out(adder_1_out), .cin(and_1_out));  // open: cout
  assign and_2_out = multiplexer_1_out & A;  // AND_Gate and_2, 8 bits wide
  assign or_1_out = multiplexer_1_out | A;  // OR_Gate or_1, 8 bits wide
  Multiplexer #(.select(2), .width(8), .enable("false")) multiplexer_2 (
    .in0(adder_1_out), .in1(and_2_out), .in2(or_1_out), .in3(adder_1_out), .out(ALU_Out), .sel(ALU_Op));

  // Notes on the sheet:
  //   8 Bit ALU
  //   00 = ADD
  //   01 = AND
  //   10 = OR
  //   11 = SUB
  //   sub not B
  //   sub cin
  //   sub
endmodule

module _8x8_bit_Register_file (
  input  [7:0] Data_In,
  input  [2:0] Read_Addr_1,
  input  Write_Enable,
  input  [2:0] Write_Addr,
  input  [2:0] Read_Addr_2,
  input  Clock,
  output [7:0] Read_1_Data,
  output [7:0] Read_2_Data
);

  wire demultiplexer_1_out0, demultiplexer_1_out1, demultiplexer_1_out2, demultiplexer_1_out3,
       demultiplexer_1_out4, demultiplexer_1_out5, demultiplexer_1_out6, demultiplexer_1_out7;
  wire [7:0] register_1_q, register_2_q, register_3_q, register_4_q, register_5_q, register_6_q,
       register_7_q, register_8_q;

  Demultiplexer #(.select(3), .enable("false")) demultiplexer_1 (
    .out0(demultiplexer_1_out0), .out1(demultiplexer_1_out1), .out2(demultiplexer_1_out2),
    .out3(demultiplexer_1_out3), .out4(demultiplexer_1_out4), .out5(demultiplexer_1_out5),
    .out6(demultiplexer_1_out6), .out7(demultiplexer_1_out7), .in(Write_Enable), .sel(Write_Addr));
  Register register_1 (.D(Data_In), .en(demultiplexer_1_out0), .Q(register_1_q), .clk(Clock));  // open: clr
  Register register_2 (.D(Data_In), .en(demultiplexer_1_out1), .Q(register_2_q), .clk(Clock));  // open: clr
  Register register_3 (.D(Data_In), .en(demultiplexer_1_out2), .Q(register_3_q), .clk(Clock));  // open: clr
  Register register_4 (.D(Data_In), .en(demultiplexer_1_out3), .Q(register_4_q), .clk(Clock));  // open: clr
  Register register_5 (.D(Data_In), .en(demultiplexer_1_out4), .Q(register_5_q), .clk(Clock));  // open: clr
  Register register_6 (.D(Data_In), .en(demultiplexer_1_out5), .Q(register_6_q), .clk(Clock));  // open: clr
  Register register_7 (.D(Data_In), .en(demultiplexer_1_out6), .Q(register_7_q), .clk(Clock));  // open: clr
  Register register_8 (.D(Data_In), .en(demultiplexer_1_out7), .Q(register_8_q), .clk(Clock));  // open: clr
  Multiplexer #(.select(3), .width(8), .enable("false")) multiplexer_1 (
    .in0(register_1_q), .in1(register_2_q), .in2(register_3_q), .in3(register_4_q), .in4(register_5_q),
    .in5(register_6_q), .in6(register_7_q), .in7(register_8_q), .out(Read_1_Data), .sel(Read_Addr_1));
  Multiplexer #(.select(3), .width(8), .enable("false")) multiplexer_2 (
    .in0(register_1_q), .in1(register_2_q), .in2(register_3_q), .in3(register_4_q), .in4(register_5_q),
    .in5(register_6_q), .in6(register_7_q), .in7(register_8_q), .out(Read_2_Data), .sel(Read_Addr_2));

  // Notes on the sheet:
  //   8x8-bit Register File
endmodule

module Control_Logic (
  input  [4:0] OPCODE,
  output IMM,
  output SW,
  output LW,
  output [1:0] OP,
  output WE1,
  output WE2
);

  or or_1 (LW, OPCODE[3], OPCODE[2]);
  not not_1 (WE1, OPCODE[3]);
  or or_2 (WE2, OPCODE[2], OPCODE[3]);

  assign IMM = OPCODE[4];
  assign OP = OPCODE[1:0];
  assign SW = OPCODE[3];
endmodule

module Full_CPU (
  input  CLK,
  output [1:0] out_2
);

  wire control_logic_1_imm, control_logic_1_lw, control_logic_1_sw, control_logic_1_we1, control_logic_1_we2;
  wire [2:0] multiplexer_1_out;
  wire [4:0] adder_1_out, register_1_q;
  wire [7:0] bit_extender_1_out, multiplexer_2_out, multiplexer_3_out, n8_bit_alu_1_alu_out,
       n8x8_bit_register_file_1_read_1_data, n8x8_bit_register_file_1_read_2_data, ram_2_data;
  wire [13:0] ram_1_data;

  Register #(.width(5)) register_1 (.D(adder_1_out), .Q(register_1_q), .clk(CLK));  // open: en, clr
  Adder #(.width(5)) adder_1 (.a(5'b00001), .b(register_1_q), .out(adder_1_out));  // open: cin, cout
  RAM #(.addrWidth(5), .dataWidth(14)) ram_1 (.addr(register_1_q), .data(ram_1_data), .clk(CLK));  // open: sel, ld, clr
  Control_Logic control_logic_1 (
    .OPCODE(ram_1_data[13:9]), .IMM(control_logic_1_imm), .SW(control_logic_1_sw), .LW(control_logic_1_lw),
    .OP(out_2), .WE1(control_logic_1_we1), .WE2(control_logic_1_we2));
  _8x8_bit_Register_file u_8x8_bit_register_file_1 (
    .Data_In(multiplexer_3_out), .Write_Enable(control_logic_1_we1), .Clock(CLK),
    .Write_Addr(ram_1_data[8:6]), .Read_Addr_1(ram_1_data[5:3]), .Read_Addr_2(multiplexer_1_out),
    .Read_1_Data(n8x8_bit_register_file_1_read_1_data), .Read_2_Data(n8x8_bit_register_file_1_read_2_data));
  Multiplexer #(.width(3), .enable("false")) multiplexer_1 (
    .in0(ram_1_data[2:0]), .in1(ram_1_data[8:6]), .out(multiplexer_1_out), .sel(control_logic_1_sw));
  assign bit_extender_1_out = {{5{ram_1_data[2]}}, ram_1_data[2:0]};  // Bit_Extender bit_extender_1
  Multiplexer #(.width(8), .enable("false")) multiplexer_2 (
    .in0(n8x8_bit_register_file_1_read_2_data), .in1(bit_extender_1_out), .out(multiplexer_2_out),
    .sel(control_logic_1_imm));
  _8_bit_ALU u_8_bit_alu_1 (
    .A(n8x8_bit_register_file_1_read_1_data), .B(multiplexer_2_out), .ALU_Op(out_2),
    .ALU_Out(n8_bit_alu_1_alu_out));
  Multiplexer #(.width(8), .enable("false")) multiplexer_3 (
    .in0(n8_bit_alu_1_alu_out), .in1(ram_2_data), .out(multiplexer_3_out), .sel(control_logic_1_lw));
  RAM #(.bus("separate")) ram_2 (
    .addr(n8_bit_alu_1_alu_out), .din(n8x8_bit_register_file_1_read_2_data), .data(ram_2_data),
    .str(control_logic_1_sw), .sel(control_logic_1_we2), .clk(CLK), .ld(control_logic_1_lw));  // open: clr

  // Notes on the sheet:
  //   src2
  //   immed select
  //   sw
  //   lw
  //   ALU op
  //   dest
  //   src1
  //   immed data
endmodule

module ALU_added (
  input  [7:0] A,
  input  [7:0] B,
  input  [2:0] ALU_Op,
  output [7:0] ALU_Out
);

  wire and_1_out;
  wire [7:0] adder_1_out, and_2_out, multiplexer_1_out, not_1_out, or_1_out, sgt_1_a_b, slt_1_slt;

  Multiplexer #(.width(8), .enable("false")) multiplexer_1 (
    .in0(B), .in1(not_1_out), .out(multiplexer_1_out), .sel(and_1_out));
  assign not_1_out = ~B;  // NOT_Gate not_1, 8 bits wide
  and and_1 (and_1_out, ALU_Op[0], ALU_Op[1]);
  Adder adder_1 (.a(A), .b(multiplexer_1_out), .out(adder_1_out), .cin(and_1_out));  // open: cout
  assign and_2_out = multiplexer_1_out & A;  // AND_Gate and_2, 8 bits wide
  assign or_1_out = multiplexer_1_out | A;  // OR_Gate or_1, 8 bits wide
  SLT slt_1 (.A(A), .B(B), .slt(slt_1_slt));
  SGT sgt_1 (.A(A), .B(B), .A_B(sgt_1_a_b));
  Multiplexer #(.select(3), .width(8), .enable("false")) multiplexer_2 (
    .in0(adder_1_out), .in1(and_2_out), .in2(or_1_out), .in3(adder_1_out), .in4(slt_1_slt), .in5(sgt_1_a_b),
    .out(ALU_Out), .sel(ALU_Op));  // open: in6, in7

  // Notes on the sheet:
  //   8 Bit ALU
  //   000 = ADD
  //   001 = AND
  //   010 = OR
  //   011 = SUB
  //   100 = SLT
  //   101 = SGT
  //   sub not B
  //   sub cin
  //   sub
endmodule

module Control_Logic___added (
  input  [7:0] OPCODE,
  output Jr,
  output J,
  output Beq,
  output IMM,
  output SW,
  output [1:0] Regifile,
  output [2:0] OP,
  output WE1,
  output WE2
);

  wire not_1_out, not_2_out, not_3_out, not_4_out;

  and and_1 (Jr, OPCODE[6], OPCODE[7]);
  not not_1 (not_1_out, OPCODE[6]);
  and and_2 (J, not_1_out, OPCODE[7]);
  and and_3 (Beq, OPCODE[6], not_2_out);
  not not_2 (not_2_out, OPCODE[7]);
  or or_1 (Regifile[0], OPCODE[4], OPCODE[3]);
  or or_2 (WE2, OPCODE[3], OPCODE[4]);
  not not_3 (not_3_out, OPCODE[4]);
  not not_4 (not_4_out, Beq);
  and and_4 (WE1, not_4_out, not_3_out);
  or or_3 (SW, Beq, OPCODE[4]);

  assign IMM = OPCODE[5];
  assign OP = OPCODE[2:0];
  assign Regifile[1] = OPCODE[7];

  // Notes on the sheet:
  //   01: beq
  //   10: j
  //   11: jr
  //   jal is j + lw
  //   Branch/Jump:
  //   00: not branch/j instruction
endmodule

module Full_CPU___added (
  input  CLK
);

  wire and_1_out, beq, control_logic_added_1_imm, control_logic_added_1_sw, control_logic_added_1_we1,
       control_logic_added_1_we2, equal0_1_out_2, jr, jump;
  wire [1:0] control_logic_added_1_regifile;
  wire [2:0] control_logic_added_1_op, multiplexer_1_out, multiplexer_2_out;
  wire [7:0] adder_2_out, alu_added_1_alu_out, bit_extender_1_out, multiplexer_3_out, multiplexer_4_out,
       multiplexer_5_out, multiplexer_6_out, multiplexer_7_out, n8x8_bit_register_file_1_read_1_data,
       n8x8_bit_register_file_1_read_2_data, ra, ram_2_data, register_1_q;
  wire [16:0] ram_1_data;

  Register register_1 (.D(multiplexer_6_out), .Q(register_1_q), .clk(CLK));  // open: en, clr
  Adder adder_1 (.a(8'h1), .b(register_1_q), .out(ra));  // open: cin, cout
  RAM #(.dataWidth(17)) ram_1 (.addr(register_1_q), .data(ram_1_data), .clk(CLK));  // open: sel, ld, clr
  Control_Logic___added control_logic_added_1 (
    .OPCODE(ram_1_data[16:9]), .Jr(jr), .J(jump), .Beq(beq), .IMM(control_logic_added_1_imm),
    .SW(control_logic_added_1_sw), .Regifile(control_logic_added_1_regifile), .OP(control_logic_added_1_op),
    .WE1(control_logic_added_1_we1), .WE2(control_logic_added_1_we2));
  Multiplexer #(.width(3), .enable("false")) multiplexer_1 (
    .in0(ram_1_data[8:6]), .in1(3'b001), .out(multiplexer_1_out), .sel(jump));
  Multiplexer #(.width(3), .enable("false")) multiplexer_2 (
    .in0(ram_1_data[2:0]), .in1(ram_1_data[8:6]), .out(multiplexer_2_out), .sel(control_logic_added_1_sw));
  _8x8_bit_Register_file u_8x8_bit_register_file_1 (
    .Data_In(multiplexer_7_out), .Write_Enable(control_logic_added_1_we1), .Clock(CLK),
    .Write_Addr(multiplexer_1_out), .Read_Addr_1(ram_1_data[5:3]), .Read_Addr_2(multiplexer_2_out),
    .Read_1_Data(n8x8_bit_register_file_1_read_1_data), .Read_2_Data(n8x8_bit_register_file_1_read_2_data));
  assign bit_extender_1_out = {{5{ram_1_data[2]}}, ram_1_data[2:0]};  // Bit_Extender bit_extender_1
  Adder adder_2 (.a(ra), .b(bit_extender_1_out), .out(adder_2_out));  // open: cin, cout
  Multiplexer #(.width(8), .enable("false")) multiplexer_3 (
    .in0(n8x8_bit_register_file_1_read_2_data), .in1(bit_extender_1_out), .out(multiplexer_3_out),
    .sel(control_logic_added_1_imm));
  ALU_added alu_added_1 (
    .A(n8x8_bit_register_file_1_read_1_data), .B(multiplexer_3_out), .ALU_Op(control_logic_added_1_op),
    .ALU_Out(alu_added_1_alu_out));
  and and_1 (and_1_out, beq, equal0_1_out_2);
  Equal0 equal0_1 (.in_1(alu_added_1_alu_out), .out_2(equal0_1_out_2));
  Multiplexer #(.width(8)) multiplexer_4 (
    .in0(ra), .in1(adder_2_out), .out(multiplexer_4_out), .sel(and_1_out));  // open: en
  Multiplexer #(.width(8)) multiplexer_5 (
    .in0(multiplexer_4_out), .in1(ram_1_data[7:0]), .out(multiplexer_5_out), .sel(jump));  // open: en
  Multiplexer #(.width(8)) multiplexer_6 (
    .in0(multiplexer_5_out), .in1(n8x8_bit_register_file_1_read_1_data), .out(multiplexer_6_out), .sel(jr));  // open: en
  RAM #(.bus("separate")) ram_2 (
    .addr(alu_added_1_alu_out), .din(n8x8_bit_register_file_1_read_2_data), .data(ram_2_data),
    .str(control_logic_added_1_sw), .sel(control_logic_added_1_we2), .clk(CLK),
    .ld(control_logic_added_1_regifile[0]));  // open: clr
  Multiplexer #(.select(2), .width(8), .enable("false")) multiplexer_7 (
    .in0(alu_added_1_alu_out), .in1(ram_2_data), .in3(ra), .out(multiplexer_7_out),
    .sel(control_logic_added_1_regifile));  // open: in2

  // Notes on the sheet:
  //   src2
  //   immed select
  //   sw
  //   rfcontrol
  //   ALU op
  //   src1
  //   dest
  //   immed data
  //   equal 0
endmodule

module Carry_Look_Ahead_Adder (
  input  c0,
  input  [7:0] A,
  input  [7:0] B,
  output S1,
  output S2,
  output S2_2,
  output S3,
  output S4,
  output S5,
  output S6,
  output S7,
  output cout
);

  wire carry_look_ahead_1_c1, carry_look_ahead_1_c2, carry_look_ahead_1_c3, carry_look_ahead_1_c4,
       carry_look_ahead_1_c5, carry_look_ahead_1_c6, carry_look_ahead_1_c7;

  Carry_Look_Ahead carry_look_ahead_1 (
    .A(A), .B(B), .c0(c0), .c1(carry_look_ahead_1_c1), .c2(carry_look_ahead_1_c2),
    .c3(carry_look_ahead_1_c3), .c4(carry_look_ahead_1_c4), .c5(carry_look_ahead_1_c5),
    .c6(carry_look_ahead_1_c6), .c7(carry_look_ahead_1_c7), .cout(cout));
  Full_Adder full_adder_1 (.A(A[0]), .B(B[0]), .Cin(c0), .Sum(S1));  // open: Cout
  Full_Adder full_adder_2 (.A(A[1]), .B(B[1]), .Cin(carry_look_ahead_1_c1), .Sum(S2));  // open: Cout
  Full_Adder full_adder_3 (.A(A[2]), .B(B[2]), .Cin(carry_look_ahead_1_c2), .Sum(S2_2));  // open: Cout
  Full_Adder full_adder_4 (.A(A[3]), .B(B[3]), .Cin(carry_look_ahead_1_c3), .Sum(S3));  // open: Cout
  Full_Adder full_adder_5 (.A(A[4]), .B(B[4]), .Cin(carry_look_ahead_1_c4), .Sum(S4));  // open: Cout
  Full_Adder full_adder_6 (.A(A[5]), .B(B[5]), .Cin(carry_look_ahead_1_c5), .Sum(S5));  // open: Cout
  Full_Adder full_adder_7 (.A(A[6]), .B(B[6]), .Cin(carry_look_ahead_1_c6), .Sum(S6));  // open: Cout
  Full_Adder full_adder_8 (.A(A[7]), .B(B[7]), .Cin(carry_look_ahead_1_c7), .Sum(S7));  // open: Cout

  // Notes on the sheet:
  //   Carry-Look Ahead Adder
endmodule

module Carry_Look_Ahead (
  input  c0,
  input  [7:0] A,
  input  [7:0] B,
  output c1,
  output c2,
  output c3,
  output c4,
  output c5,
  output c6,
  output c7,
  output cout
);

  wire and_7_out, and_10_out, and_11_out, and_12_out, and_13_out, and_14_out, and_15_out, and_16_out,
       and_17_out, and_18_out, and_19_out, and_20_out, and_21_out, and_22_out, and_23_out, and_24_out,
       and_25_out, and_26_out, and_27_out, and_28_out, and_29_out, and_30_out, and_31_out, and_32_out,
       and_33_out, and_34_out, and_35_out, and_36_out, and_37_out, and_38_out, and_39_out, and_40_out,
       and_41_out, and_42_out, and_43_out, and_44_out, g0, g1, g2, g3, g4, g5, g6, g7, p0, p1, p2, p3, p4,
       p5, p6, p7;

  and and_1 (g7, A[7], B[7]);
  and and_2 (g0, A[0], B[0]);
  xor xor_1 (p0, A[0], B[0]);
  and and_3 (g1, A[1], B[1]);
  and and_4 (g2, A[2], B[2]);
  and and_5 (g5, A[5], B[5]);
  xor xor_2 (p5, A[5], B[5]);
  and and_6 (g6, A[6], B[6]);
  xor xor_3 (p6, A[6], B[6]);
  xor xor_4 (p7, A[7], B[7]);
  and and_7 (and_7_out, c0, p0);
  xor xor_5 (p1, A[1], B[1]);
  xor xor_6 (p2, A[2], B[2]);
  and and_8 (g3, A[3], B[3]);
  xor xor_7 (p3, A[3], B[3]);
  and and_9 (g4, A[4], B[4]);
  xor xor_8 (p4, A[4], B[4]);
  and and_10 (and_10_out, p7, g6);
  and and_11 (and_11_out, p1, g0);
  and and_12 (and_12_out, p1, p0, c0);
  and and_13 (and_13_out, p2, g1);
  and and_14 (and_14_out, p5, g4);
  and and_15 (and_15_out, p5, p4, g3);
  and and_16 (and_16_out, p5, p4, p3, g2);
  and and_17 (and_17_out, p6, g5);
  and and_18 (and_18_out, p6, p5, g4);
  and and_19 (and_19_out, p6, p5, p4, g3);
  and and_20 (and_20_out, p6, p5, p4, p3, g2);
  and and_21 (and_21_out, p6, p5, p4, p3, p2, g1);
  and and_22 (and_22_out, p6, p5, p4, p3, p2, p1, g0);
  and and_23 (and_23_out, p6, p5, p4, p3, p2, p1, p0, c0);
  and and_24 (and_24_out, p7, p6, g5);
  and and_25 (and_25_out, p7, p6, p5, g4);
  and and_26 (and_26_out, p7, p6, p5, p4, g3);
  and and_27 (and_27_out, p7, p6, p5, p4, p3, g2);
  and and_28 (and_28_out, p7, p6, p5, p4, p3, p2, g1);
  and and_29 (and_29_out, p7, p6, p5, p4, p3, p2, p1, g0);
  and and_30 (and_30_out, p7, p6, p5, p4, p3, p2, p1, p0, c0);
  and and_31 (and_31_out, p2, p1, g0);
  and and_32 (and_32_out, p2, p1, p0, c0);
  and and_33 (and_33_out, p3, g2);
  and and_34 (and_34_out, p3, p2, g1);
  and and_35 (and_35_out, p3, p2, p1, g0);
  and and_36 (and_36_out, p3, p2, p1, p0, c0);
  and and_37 (and_37_out, p4, g3);
  and and_38 (and_38_out, p4, p3, g2);
  and and_39 (and_39_out, p4, p3, p2, g1);
  and and_40 (and_40_out, p4, p3, p2, p1, p0, c0);
  and and_41 (and_41_out, p5, p4, p3, p2, g1);
  and and_42 (and_42_out, p5, p4, p3, p2, p1, g0);
  and and_43 (and_43_out, p5, p4, p3, p2, p1, p0, c0);
  and and_44 (and_44_out, p4, p3, p2, p1, g0);
  or or_1 (c1, g0, and_7_out);
  or or_2 (c2, g1, and_11_out, and_12_out);
  or or_3 (c3, g2, and_13_out, and_31_out, and_32_out);
  or or_4 (c4, g3, and_33_out, and_34_out, and_35_out, and_36_out);
  or or_5 (c5, g4, and_37_out, and_38_out, and_39_out, and_44_out, and_40_out);
  or or_6 (c6, g5, and_14_out, and_15_out, and_16_out, and_41_out, and_42_out, and_43_out);
  or or_7 (c7, g6, and_17_out, and_18_out, and_19_out, and_20_out, and_21_out, and_22_out, and_23_out);
  or or_8 (cout, g7, and_10_out, and_24_out, and_25_out, and_26_out, and_27_out, and_28_out, and_29_out, and_30_out);

  // Notes on the sheet:
  //   Carry-Look Ahead
endmodule

module SLT (
  input  [7:0] A,
  input  [7:0] B,
  output [7:0] slt
);

  wire and_1_out, and_7_out, and_8_out, and_9_out, and_10_out, and_11_out, and_12_out, and_13_out, eq1, eq2,
       eq3, eq4, eq5, eq6, x_y_1_out_3, x_y_2_out_3, x_y_3_out_3, x_y_4_out_3, x_y_5_out_3, x_y_6_out_3,
       x_y_7_out_3, x_y_8_out_3, xnor_2_out, xnor_3_out, xnor_4_out, xnor_5_out, xnor_6_out, xnor_7_out;

  X_Y x_y_1 (.in_1(B[7]), .in_2(A[7]), .out_3(x_y_1_out_3));
  xnor xnor_1 (eq1, A[7], B[7]);
  X_Y x_y_2 (.in_1(A[6]), .in_2(B[6]), .out_3(x_y_2_out_3));
  xnor xnor_2 (xnor_2_out, A[6], B[6]);
  X_Y x_y_3 (.in_1(A[5]), .in_2(B[5]), .out_3(x_y_3_out_3));
  xnor xnor_3 (xnor_3_out, A[5], B[5]);
  X_Y x_y_4 (.in_1(A[4]), .in_2(B[4]), .out_3(x_y_4_out_3));
  xnor xnor_4 (xnor_4_out, A[4], B[4]);
  X_Y x_y_5 (.in_1(A[3]), .in_2(B[3]), .out_3(x_y_5_out_3));
  xnor xnor_5 (xnor_5_out, A[3], B[3]);
  X_Y x_y_6 (.in_1(A[2]), .in_2(B[2]), .out_3(x_y_6_out_3));
  xnor xnor_6 (xnor_6_out, A[2], B[2]);
  X_Y x_y_7 (.in_1(A[1]), .in_2(B[1]), .out_3(x_y_7_out_3));
  xnor xnor_7 (xnor_7_out, A[1], B[1]);
  X_Y x_y_8 (.in_1(A[0]), .in_2(B[0]), .out_3(x_y_8_out_3));
  and and_1 (and_1_out, eq1, x_y_2_out_3);
  and and_2 (eq2, eq1, xnor_2_out);
  and and_3 (eq3, eq2, xnor_3_out);
  and and_4 (eq4, eq3, xnor_4_out);
  and and_5 (eq5, eq4, xnor_5_out);
  and and_6 (eq6, eq5, xnor_6_out);
  and and_7 (and_7_out, eq6, xnor_7_out);
  and and_8 (and_8_out, eq2, x_y_3_out_3);
  and and_9 (and_9_out, eq3, x_y_4_out_3);
  and and_10 (and_10_out, eq4, x_y_5_out_3);
  and and_11 (and_11_out, eq5, x_y_6_out_3);
  and and_12 (and_12_out, eq6, x_y_7_out_3);
  and and_13 (and_13_out, and_7_out, x_y_8_out_3);
  or or_1 (slt[0], x_y_1_out_3, and_1_out, and_8_out, and_9_out, and_10_out, and_11_out, and_12_out, and_13_out);

  assign slt[7:1] = {7{1'b0}};
endmodule

module SGT (
  input  [7:0] A,
  input  [7:0] B,
  output [7:0] A_B
);

  wire and_1_out, equal0_1_out_2, equal0_2_out_2, equal0_3_out_2, not_2_out, or_1_out;
  wire [7:0] not_1_out, slt_1_slt, subtractor_1_out;

  SLT slt_1 (.A(A), .B(B), .slt(slt_1_slt));
  Equal0 equal0_1 (.in_1(A), .out_2(equal0_1_out_2));
  Equal0 equal0_2 (.in_1(B), .out_2(equal0_2_out_2));
  Equal0 equal0_3 (.in_1(subtractor_1_out), .out_2(equal0_3_out_2));
  Subtractor subtractor_1 (.a(A), .b(B), .out(subtractor_1_out));  // open: bin, bout
  and and_1 (and_1_out, equal0_1_out_2, equal0_2_out_2);
  assign not_1_out = ~slt_1_slt;  // NOT_Gate not_1, 8 bits wide
  or or_1 (or_1_out, and_1_out, equal0_3_out_2);
  not not_2 (not_2_out, or_1_out);
  and and_2 (A_B[0], not_1_out[0], not_2_out);

  assign A_B[7:1] = {7{1'b0}};

  // Notes on the sheet:
  //   Output = 1 if A > B
  //   check if A=B
endmodule

module Full_Adder (
  input  A,
  input  B,
  input  Cin,
  output Sum,
  output Cout
);

  wire half_adder_1_cout, half_adder_1_sum, half_adder_2_cout;

  Half_Adder half_adder_1 (.A(A), .B(B), .Sum(half_adder_1_sum), .Cout(half_adder_1_cout));
  Half_Adder half_adder_2 (.A(half_adder_1_sum), .B(Cin), .Sum(Sum), .Cout(half_adder_2_cout));
  or or_1 (Cout, half_adder_2_cout, half_adder_1_cout);

  // Notes on the sheet:
  //   Full Adder
endmodule

module Half_Adder (
  input  A,
  input  B,
  output Sum,
  output Cout
);

  xor xor_1 (Sum, A, B);
  and and_1 (Cout, A, B);

  // Notes on the sheet:
  //   Half Adder
endmodule

module X_Y (
  input  in_1,
  input  in_2,
  output out_3
);

  wire not_1_out;

  not not_1 (not_1_out, in_1);
  and and_1 (out_3, not_1_out, in_2);
endmodule

module Equal0 (
  input  [7:0] in_1,
  output out_2
);

  wire [7:0] not_1_out;

  assign not_1_out = ~in_1;  // NOT_Gate not_1, 8 bits wide
  and and_1 (out_2, not_1_out[0], not_1_out[1], not_1_out[2], not_1_out[3], not_1_out[4], not_1_out[5], not_1_out[6], not_1_out[7]);
endmodule
